# Fritzing sketch circuit (saved by Fritzing 0.9.4)

parts:
  Raspberry_Pi_1 = Raspberry Pi 3 [part_number=RPI-3-V1.2]
  Part1 = Adafruit DC+Stepper Motor HAT [part_number="Adafruit #2348"]
  M1 = DC Motor
  M2 = DC Motor
  J1 = Basic Servo
  VCC1 = 4 x AAA Battery Mount

nets (from the schematic view):
  N1: Raspberry_Pi_1.GPIO2, Part1.SDA
  N2: Raspberry_Pi_1.GPIO3, Part1.SCL
  N3: Raspberry_Pi_1.GPIO4, Part1.GPIO4
  N4: Raspberry_Pi_1.GPIO17, Part1.GPIO17
  N5: Raspberry_Pi_1.GPIO27, Part1.GPIO27
  N6: Raspberry_Pi_1.GPIO22, Part1.GPIO22
  3V3: Raspberry_Pi_1.3V3, Part1.3.3V, J1.vcc
  N7: Raspberry_Pi_1.GPIO10, Part1.SPI_MOSI
  N8: Raspberry_Pi_1.GPIO9, Part1.SPI_MISO
  N9: Raspberry_Pi_1.GPIO11, Part1.SPI_SCLK
  N10: Raspberry_Pi_1.GPIO5, Part1.GPIO5
  N11: Raspberry_Pi_1.GPIO6, Part1.GPIO6
  N12: Raspberry_Pi_1.GPIO13, Part1.GPIO13
  N13: Raspberry_Pi_1.GPIO19, Part1.GPIO19
  N14: Raspberry_Pi_1.GPIO26, Part1.GPIO26
  N15: Raspberry_Pi_1.GPIO21, Part1.GPIO21
  N16: Raspberry_Pi_1.GPIO20, Part1.GPIO20, J1.pulse
  N17: Raspberry_Pi_1.GPIO16, Part1.GPIO16
  GND: Raspberry_Pi_1.GND, Part1.GND, J1.gnd, VCC1.-
  N18: Raspberry_Pi_1.GPIO12, Part1.GPIO12
  N19: Raspberry_Pi_1.GPIO7, Part1.SPI_CE1
  N20: Raspberry_Pi_1.GPIO8, Part1.SPI_CE0
  N21: Raspberry_Pi_1.GPIO25, Part1.GPIO25
  N22: Raspberry_Pi_1.GPIO24, Part1.GPIO24
  N23: Raspberry_Pi_1.GPIO23, Part1.GPIO23
  N24: Raspberry_Pi_1.GPIO18, Part1.GPIO18
  N25: Raspberry_Pi_1.GPIO15, Part1.RXD
  N26: Raspberry_Pi_1.GPIO14, Part1.TXD
  N27: Raspberry_Pi_1.5V, Part1.5.0V
  N28: Part1.M2A, M2.pin_2
  N29: Part1.M2B, M2.pin_1
  N30: Part1.M1B, M1.pin_1
  N31: Part1.M1A, M1.pin_2
  N32: Part1.VMOTOR, VCC1.+

custom parts:
  Adafruit DC+Stepper Motor HAT: Let your robotic dreams come true with the new DC+Stepper Motor HAT from Adafruit. This Raspberry Pi add-on is perfect for any motion project as it can drive up to 4 DC or 2 Stepper motors with full PWM speed control. Since the Raspberry Pi does not have a lot of PWM pins, we use a fully-dedicated PWM driver chip onboard to both control motor direction and speed. This chip handles all the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
